// Logisim project control-logic.circ as structural Verilog: 1 circuit, main circuit control_logic
module control_logic (
  input  [31:0] Instruction,
  input  BrEq,
  input  BrLt,
  output PCSel,
  output RegWEn,
  output [2:0] ImmSel,
  output BrUn,
  output ASel,
  output BSel,
  output [3:0] ALUSel,
  output MemRW,
  output [1:0] WBSel
);

  wire and_2_out, and_3_out, and_4_out, and_5_out, and_6_out, and_7_out, Bopcode, comparator_7_eq,
       comparator_8_eq, comparator_11_eq, comparator_12_eq, comparator_13_eq, comparator_14_eq,
       comparator_15_eq, comparator_16_eq, comparator_17_eq, comparator_18_eq, comparator_19_eq,
       comparator_20_eq, comparator_21_eq, comparator_22_eq, comparator_23_eq, comparator_24_eq,
       demultiplexer_1_out1, demultiplexer_1_out5, demultiplexer_2_out0, Iopcode, is_add, is_addi, is_and,
       is_andi, is_auipc, is_beq, is_bge, is_bgeu, is_blt, is_bltu, is_bne, is_jal, is_jalr, is_lb, is_lh,
       is_lui, is_lw, is_mul, is_mulh, is_mulhu, is_or, is_ori, is_sb, is_sh, is_sll, is_slli, is_slt,
       is_slti, is_sra, is_srai, is_srl, is_srli, is_sub, is_sw, is_xor, is_xori, Lopcode, not_1_out,
       not_2_out, not_3_out, or_1_out, or_2_out, or_3_out, or_4_out, or_5_out, or_6_out, R_1, R_2, R_3, R_4,
       R_5, R_6, R_7, Ropcode, Sopcode;
  wire [5:0] ROM_Input;
  wire [15:14] rom_1_data;

  ROM #(.addrWidth(6), .dataWidth(16)) rom_1 (
    .addr(ROM_Input), .data({rom_1_data, WBSel, MemRW, ALUSel, BSel, ASel, BrUn, ImmSel, RegWEn}));
  Priority_Encoder #(.select_enc(6)) priority_encoder_1 (
    .in0(is_add), .in1(is_mul), .in2(is_sub), .in3(is_sll), .in4(is_mulh), .in5(is_mulhu), .in6(is_slt),
    .in7(is_xor), .in8(is_srl), .in9(is_sra), .in10(is_or), .in11(is_and), .in12(is_lb), .in13(is_lh),
    .in14(is_lw), .in15(is_addi), .in16(is_slli), .in17(is_slti), .in18(is_xori), .in19(is_srli),
    .in20(is_srai), .in21(is_ori), .in22(is_andi), .in23(is_sb), .in24(is_sh), .in25(is_sw), .in26(is_beq),
    .in27(is_bne), .in28(is_blt), .in29(is_bge), .in30(is_bltu), .in31(is_bgeu), .in32(is_auipc),
    .in33(is_lui), .in34(is_jal), .in35(is_jalr), .out(ROM_Input));  // open: in36, in37, in38, in39, in40, in41, in42, in43, in44, in45, in46, in47, in48, in49, in50, in51, in52, in53, in54, in55, in56, in57, in58, in59, in60, in61, in62, in63, gs, en_out, en_in
  Comparator #(.width(7)) comparator_1 (.a(Instruction[6:0]), .b(7'b0010011), .eq(Iopcode));  // open: gt, lt
  Comparator #(.width(7)) comparator_2 (.a(Instruction[6:0]), .b(7'b0110011), .eq(Ropcode));  // open: gt, lt
  Comparator #(.width(7)) comparator_3 (.a(Instruction[6:0]), .b(7'b1100011), .eq(Bopcode));  // open: gt, lt
  Comparator #(.width(7)) comparator_4 (.a(Instruction[6:0]), .b(7'b0000011), .eq(Lopcode));  // open: gt, lt
  Comparator #(.width(7)) comparator_5 (.a(Instruction[6:0]), .b(7'b0100011), .eq(Sopcode));  // open: gt, lt
  Comparator #(.width(7)) comparator_6 (.a(Instruction[6:0]), .b(7'b1101111), .eq(is_jal));  // open: gt, lt
  Comparator #(.width(7)) comparator_7 (.a(Instruction[6:0]), .b(7'b1100111), .eq(comparator_7_eq));  // open: gt, lt
  Comparator #(.width(3)) comparator_8 (.a(Instruction[14:12]), .b(3'b000), .eq(comparator_8_eq));  // open: gt, lt
  Comparator #(.width(7)) comparator_9 (.a(Instruction[6:0]), .b(7'b0010111), .eq(is_auipc));  // open: gt, lt
  Comparator #(.width(7)) comparator_10 (.a(Instruction[6:0]), .b(7'b0110111), .eq(is_lui));  // open: gt, lt
  and and_1 (is_jalr, comparator_7_eq, comparator_8_eq);
  and and_2 (and_2_out, is_beq, BrEq);
  and and_3 (and_3_out, is_bne, not_1_out);
  not not_1 (not_1_out, BrEq);
  and and_4 (and_4_out, is_blt, BrLt);
  and and_5 (and_5_out, is_bge, not_2_out);
  not not_2 (not_2_out, BrLt);
  and and_6 (and_6_out, is_bltu, BrLt);
  and and_7 (and_7_out, is_bgeu, not_3_out);
  not not_3 (not_3_out, BrLt);
  Demultiplexer #(.select(3)) demultiplexer_1 (
    .out0(is_addi), .out1(demultiplexer_1_out1), .out2(is_slti), .out4(is_xori), .out5(demultiplexer_1_out5),
    .out6(is_ori), .out7(is_andi), .in(Iopcode), .sel(Instruction[14:12]));  // open: out3
  Demultiplexer #(.select(3)) demultiplexer_2 (
    .out0(demultiplexer_2_out0), .out1(R_1), .out2(R_2), .out3(R_3), .out4(R_4), .out5(R_5), .out6(R_6),
    .out7(R_7), .in(Ropcode), .sel(Instruction[14:12]));
  Demultiplexer #(.select(3)) demultiplexer_3 (
    .out0(is_beq), .out1(is_bne), .out4(is_blt), .out5(is_bge), .out6(is_bltu), .out7(is_bgeu), .in(Bopcode),
    .sel(Instruction[14:12]));  // open: out2, out3
  Demultiplexer #(.select(3)) demultiplexer_4 (
    .out0(is_lb), .out1(is_lh), .out2(is_lw), .in(Lopcode), .sel(Instruction[14:12]));  // open: out3, out4, out5, out6, out7
  Demultiplexer #(.select(3)) demultiplexer_5 (
    .out0(is_sb), .out1(is_sh), .out2(is_sw), .in(Sopcode), .sel(Instruction[14:12]));  // open: out3, out4, out5, out6, out7
  or or_1 (or_1_out, and_2_out, and_3_out);
  or or_2 (or_2_out, and_4_out, and_5_out);
  or or_3 (or_3_out, and_6_out, and_7_out);
  or or_4 (or_4_out, or_1_out, or_2_out);
  Comparator #(.width(7)) comparator_11 (.a({7{1'b0}}), .b(Instruction[31:25]), .eq(comparator_11_eq));  // open: gt, lt
  Comparator #(.width(7)) comparator_12 (
    .a(7'b0100000), .b(Instruction[31:25]), .eq(comparator_12_eq));  // open: gt, lt
  Comparator #(.width(7)) comparator_13 (
    .a(Instruction[31:25]), .b(7'b0000001), .eq(comparator_13_eq));  // open: gt, lt
  or or_5 (or_5_out, or_4_out, or_3_out);
  or or_6 (or_6_out, is_jal, is_jalr);
  Comparator #(.width(7)) comparator_14 (.a({7{1'b0}}), .b(Instruction[31:25]), .eq(comparator_14_eq));  // open: gt, lt
  and and_8 (is_slli, comparator_14_eq, demultiplexer_1_out1);
  and and_9 (is_add, demultiplexer_2_out0, comparator_11_eq);
  and and_10 (is_sub, demultiplexer_2_out0, comparator_12_eq);
  and and_11 (is_mul, demultiplexer_2_out0, comparator_13_eq);
  or or_7 (PCSel, or_5_out, or_6_out);
  and and_12 (is_srli, comparator_14_eq, demultiplexer_1_out5);
  Comparator #(.width(7)) comparator_15 (
    .a(7'b0000001), .b(Instruction[31:25]), .eq(comparator_15_eq));  // open: gt, lt
  Comparator #(.width(7)) comparator_16 (.a({7{1'b0}}), .b(Instruction[31:25]), .eq(comparator_16_eq));  // open: gt, lt
  Comparator #(.width(7)) comparator_17 (.a({7{1'b0}}), .b(Instruction[31:25]), .eq(comparator_17_eq));  // open: gt, lt
  Comparator #(.width(7)) comparator_18 (
    .a(7'b0000001), .b(Instruction[31:25]), .eq(comparator_18_eq));  // open: gt, lt
  Comparator #(.width(7)) comparator_19 (.a({7{1'b0}}), .b(Instruction[31:25]), .eq(comparator_19_eq));  // open: gt, lt
  Comparator #(.width(7)) comparator_20 (.a({7{1'b0}}), .b(Instruction[31:25]), .eq(comparator_20_eq));  // open: gt, lt
  Comparator #(.width(7)) comparator_21 (
    .a(7'b0100000), .b(Instruction[31:25]), .eq(comparator_21_eq));  // open: gt, lt
  Comparator #(.width(7)) comparator_22 (.a({7{1'b0}}), .b(Instruction[31:25]), .eq(comparator_22_eq));  // open: gt, lt
  Comparator #(.width(7)) comparator_23 (.a({7{1'b0}}), .b(Instruction[31:25]), .eq(comparator_23_eq));  // open: gt, lt
  Comparator #(.width(7)) comparator_24 (
    .a(7'b0100000), .b(Instruction[31:25]), .eq(comparator_24_eq));  // open: gt, lt
  and and_13 (is_mulh, R_1, comparator_15_eq);
  and and_14 (is_sll, R_1, comparator_16_eq);
  and and_15 (is_slt, R_2, comparator_17_eq);
  and and_16 (is_mulhu, R_3, comparator_18_eq);
  and and_17 (is_xor, R_4, comparator_19_eq);
  and and_18 (is_srl, R_5, comparator_20_eq);
  and and_19 (is_sra, R_5, comparator_21_eq);
  and and_20 (is_or, R_6, comparator_22_eq);
  and and_21 (is_and, R_7, comparator_23_eq);
  and and_22 (is_srai, comparator_24_eq, demultiplexer_1_out5);

  // Other names for the same wires on the sheet: BFunct3[2:0] = Instruction[14:12]; IFunct3[2:0] = Instruction[14:12];
  //   LFunct3[2:0] = Instruction[14:12]; RFunct3[2:0] = Instruction[14:12]; SFunct3[2:0] = Instruction[14:12];
  //   IFunct7[6:0] = Instruction[31:25]; RFunct7[6:0] = Instruction[31:25]

  // Notes on the sheet:
  //   INPUTS to your circuit
  //   contents of rom_1 (hex, n*v repeats v):
  //   1003 1403 1603 1083 1483 1583 1103 1203 1283 1683 1303 1383 841 841 841 1041 10c1 1141 1241 12c1
  //   16c1 1341 13c1 842 842 842 4*64 74 74 1067 17c7 2069 2041
  //   ROM FOR CONTROL LOGIC
  //   DON'T CHANGE THE LOCATIONS OF THE INPUTS AND OUTPUTS!
  //   This is only if you choose to do the ROM option
  //   OUTPUT from your circuit
  //   Reminder: If using ROM, use combinational logic for PCSel
endmodule
