// Logisim project partial-load.circ as structural Verilog: 1 circuit, main circuit partial_load
module partial_load (
  input  [31:0] Instruction,
  input  [31:0] MemAddress,
  input  [31:0] DataFromMem,
  output [31:0] DataToReg
);

  wire Lopcode;
  wire [31:0] lb00, lb01, lb02, lb03, lh00, lh01, lh02, multiplexer_1_out;

  Multiplexer #(.select(5), .width(32)) multiplexer_1 (
    .in0(lb00), .in1(lb01), .in2(lb02), .in3(lb03), .in4(lh00), .in5(lh01), .in6(lh02), .in8(DataFromMem),
    .out(multiplexer_1_out), .sel({Instruction[14:12], MemAddress[1:0]}));  // open: in7, in9, in10, in11, in12, in13, in14, in15, in16, in17, in18, in19, in20, in21, in22, in23, in24, in25, in26, in27, in28, in29, in30, in31
  Comparator #(.width(7)) comparator_1 (.a(7'b0000011), .b(Instruction[6:0]), .eq(Lopcode));  // open: gt, lt
  assign lb00 = {{24{DataFromMem[7]}}, DataFromMem[7:0]};  // Bit_Extender bit_extender_1
  assign lb01 = {{24{DataFromMem[15]}}, DataFromMem[15:8]};  // Bit_Extender bit_extender_2
  assign lb02 = {{24{DataFromMem[23]}}, DataFromMem[23:16]};  // Bit_Extender bit_extender_3
  assign lb03 = {{24{DataFromMem[31]}}, DataFromMem[31:24]};  // Bit_Extender bit_extender_4
  assign lh00 = {{16{DataFromMem[15]}}, DataFromMem[15:0]};  // Bit_Extender bit_extender_5
  assign lh01 = {{16{DataFromMem[23]}}, DataFromMem[23:8]};  // Bit_Extender bit_extender_6
  assign lh02 = {{16{DataFromMem[31]}}, DataFromMem[31:16]};  // Bit_Extender bit_extender_7
  Multiplexer #(.width(32)) multiplexer_2 (.in1(multiplexer_1_out), .out(DataToReg), .sel(Lopcode));  // open: in0

  // Other names for the same wires on the sheet: LMux[4:0] = {Instruction[14:12], MemAddress[1:0]};
  //   lw[31:0] = DataFromMem

  // Notes on the sheet:
  //   INPUTS to your circuit
  //   DON'T CHANGE THE LOCATIONS OF THE INPUTS AND OUTPUTS!
  //   OUTPUT from your circuit
endmodule
