// Logisim project partial-store.circ as structural Verilog: 1 circuit, main circuit partial_store
module partial_store (
  input  [31:0] Instruction,
  input  [31:0] MemAddress,
  input  [31:0] DataFromReg,
  input  MemRW,
  output [3:0] MemWriteMask,
  output [31:0] DataToMem
);

  wire Sopcode;
  wire [3:0] multiplexer_4_out, multiplexer_5_out;
  wire [31:0] multiplexer_1_out, multiplexer_2_out;

  Multiplexer #(.select(5), .width(32)) multiplexer_1 (
    .in0({{24{1'b0}}, DataFromReg[7:0]}), .in1({{16{1'b0}}, DataFromReg[7:0], {8{1'b0}}}),
    .in2({{8{1'b0}}, DataFromReg[7:0], {16{1'b0}}}), .in3({DataFromReg[7:0], {24{1'b0}}}),
    .in4({{16{1'b0}}, DataFromReg[15:0]}), .in6({DataFromReg[15:0], {16{1'b0}}}), .in8(DataFromReg),
    .out(multiplexer_1_out), .sel({Instruction[14:12], MemAddress[1:0]}));  // open: in5, in7, in9, in10, in11, in12, in13, in14, in15, in16, in17, in18, in19, in20, in21, in22, in23, in24, in25, in26, in27, in28, in29, in30, in31
  Multiplexer #(.width(32)) multiplexer_2 (
    .in1(multiplexer_1_out), .out(multiplexer_2_out), .sel(Sopcode));  // open: in0
  Comparator #(.width(7)) comparator_1 (.a(7'b0100011), .b(Instruction[6:0]), .eq(Sopcode));  // open: gt, lt
  Multiplexer #(.width(32)) multiplexer_3 (.in1(multiplexer_2_out), .out(DataToMem), .sel(MemRW));  // open: in0
  Multiplexer #(.select(5), .width(4)) multiplexer_4 (
    .in0(4'b0001), .in1(4'b0010), .in2(4'b0100), .in3(4'b1000), .in4(4'b0011), .in6(4'b1100), .in8(4'b1111),
    .out(multiplexer_4_out), .sel({Instruction[14:12], MemAddress[1:0]}));  // open: in5, in7, in9, in10, in11, in12, in13, in14, in15, in16, in17, in18, in19, in20, in21, in22, in23, in24, in25, in26, in27, in28, in29, in30, in31
  Multiplexer #(.width(4)) multiplexer_5 (
    .in0(4'b0000), .in1(multiplexer_4_out), .out(multiplexer_5_out), .sel(Sopcode));
  Multiplexer #(.width(4)) multiplexer_6 (.in0(4'b0000), .in1(multiplexer_5_out), .out(MemWriteMask), .sel(MemRW));

  // Other names for the same wires on the sheet: sb00[7:0] = DataFromReg[7:0]; sb01[15:8] = DataFromReg[7:0];
  //   sb02[23:16] = DataFromReg[7:0]; sb03[31:24] = DataFromReg[7:0]; sh00[15:0] = DataFromReg[15:0];
  //   sh01[31:16] = DataFromReg[15:0]; SMux[4:0] = {Instruction[14:12], MemAddress[1:0]}

  // Notes on the sheet:
  //   INPUTS to your circuit
  //   DON'T CHANGE THE LOCATIONS OF THE INPUTS AND OUTPUTS!
  //   OUTPUT from your circuit
endmodule
