// Logisim project regfile.circ as structural Verilog: 1 circuit, main circuit regfile
module regfile (
  input  [4:0] ReadIndex1,
  input  [4:0] ReadIndex2,
  input  [4:0] WriteIndex,
  input  [31:0] WriteData,
  input  RegWEn,
  input  clk,
  output [31:0] ra,
  output [31:0] sp,
  output [31:0] t0,
  output [31:0] t1,
  output [31:0] t2,
  output [31:0] s0,
  output [31:0] s1,
  output [31:0] a0,
  output [31:0] ReadData1,
  output [31:0] ReadData2
);

  wire x0w, x1w, x2w, x3w, x4w, x5w, x6w, x7w, x8w, x9w, x10w, x11w, x12w, x13w, x14w, x15w, x16w, x17w,
       x18w, x19w, x20w, x21w, x22w, x23w, x24w, x25w, x26w, x27w, x28w, x29w, x30w, x31w;
  wire [31:0] a1, a2, a3, a4, a5, a6, a7, gp, mux1, mux2, mux21, mux22, s2, s3, s4, s5, s6, s7, s8, s9, s10,
       s11, t3, t4, t5, t6, tp, x0;

  Register #(.width(32)) u_x0 (.D({32{1'b0}}), .en(x0w), .clk(clk), .Q(x0));  // open: clr
  Register #(.width(32)) x1 (.D(WriteData), .en(x1w), .clk(clk), .Q(ra));  // open: clr
  Register #(.width(32)) x2 (.D(WriteData), .en(x2w), .clk(clk), .Q(sp));  // open: clr
  Register #(.width(32)) x3 (.D(WriteData), .en(x3w), .clk(clk), .Q(gp));  // open: clr
  Register #(.width(32)) x4 (.D(WriteData), .en(x4w), .clk(clk), .Q(tp));  // open: clr
  Register #(.width(32)) x5 (.D(WriteData), .en(x5w), .clk(clk), .Q(t0));  // open: clr
  Register #(.width(32)) x6 (.D(WriteData), .en(x6w), .clk(clk), .Q(t1));  // open: clr
  Register #(.width(32)) x7 (.D(WriteData), .en(x7w), .clk(clk), .Q(t2));  // open: clr
  Register #(.width(32)) x8 (.D(WriteData), .en(x8w), .clk(clk), .Q(s0));  // open: clr
  Register #(.width(32)) x9 (.D(WriteData), .en(x9w), .clk(clk), .Q(s1));  // open: clr
  Register #(.width(32)) x10 (.D(WriteData), .en(x10w), .clk(clk), .Q(a0));  // open: clr
  Register #(.width(32)) x11 (.D(WriteData), .en(x11w), .clk(clk), .Q(a1));  // open: clr
  Register #(.width(32)) x12 (.D(WriteData), .en(x12w), .clk(clk), .Q(a2));  // open: clr
  Register #(.width(32)) x13 (.D(WriteData), .en(x13w), .clk(clk), .Q(a3));  // open: clr
  Register #(.width(32)) x14 (.D(WriteData), .en(x14w), .clk(clk), .Q(a4));  // open: clr
  Register #(.width(32)) x15 (.D(WriteData), .en(x15w), .clk(clk), .Q(a5));  // open: clr
  Multiplexer #(.select(4), .width(32)) multiplexer_1 (
    .in0(x0), .in1(ra), .in2(sp), .in3(gp), .in4(tp), .in5(t0), .in6(t1), .in7(t2), .in8(s0), .in9(s1),
    .in10(a0), .in11(a1), .in12(a2), .in13(a3), .in14(a4), .in15(a5), .out(mux1), .sel(ReadIndex1[3:0]));
  Multiplexer #(.width(32)) multiplexer_2 (.in0(mux1), .in1(mux2), .out(ReadData1), .sel(ReadIndex1[4]));
  Register #(.width(32)) x16 (.D(WriteData), .en(x16w), .clk(clk), .Q(a6));  // open: clr
  Register #(.width(32)) x17 (.D(WriteData), .en(x17w), .clk(clk), .Q(a7));  // open: clr
  Register #(.width(32)) x18 (.D(WriteData), .en(x18w), .clk(clk), .Q(s2));  // open: clr
  Register #(.width(32)) x19 (.D(WriteData), .en(x19w), .clk(clk), .Q(s3));  // open: clr
  Register #(.width(32)) x20 (.D(WriteData), .en(x20w), .clk(clk), .Q(s4));  // open: clr
  Register #(.width(32)) x21 (.D(WriteData), .en(x21w), .clk(clk), .Q(s5));  // open: clr
  Register #(.width(32)) x22 (.D(WriteData), .en(x22w), .clk(clk), .Q(s6));  // open: clr
  Register #(.width(32)) x23 (.D(WriteData), .en(x23w), .clk(clk), .Q(s7));  // open: clr
  Register #(.width(32)) x24 (.D(WriteData), .en(x24w), .clk(clk), .Q(s8));  // open: clr
  Register #(.width(32)) x25 (.D(WriteData), .en(x25w), .clk(clk), .Q(s9));  // open: clr
  Register #(.width(32)) x26 (.D(WriteData), .en(x26w), .clk(clk), .Q(s10));  // open: clr
  Register #(.width(32)) x27 (.D(WriteData), .en(x27w), .clk(clk), .Q(s11));  // open: clr
  Register #(.width(32)) x28 (.D(WriteData), .en(x28w), .clk(clk), .Q(t3));  // open: clr
  Register #(.width(32)) x29 (.D(WriteData), .en(x29w), .clk(clk), .Q(t4));  // open: clr
  Register #(.width(32)) x30 (.D(WriteData), .en(x30w), .clk(clk), .Q(t5));  // open: clr
  Register #(.width(32)) x31 (.D(WriteData), .en(x31w), .clk(clk), .Q(t6));  // open: clr
  Multiplexer #(.select(4), .width(32)) multiplexer_3 (
    .in0(a6), .in1(a7), .in2(s2), .in3(s3), .in4(s4), .in5(s5), .in6(s6), .in7(s7), .in8(s8), .in9(s9),
    .in10(s10), .in11(s11), .in12(t3), .in13(t4), .in14(t5), .in15(t6), .out(mux2), .sel(ReadIndex1[3:0]));
  Multiplexer #(.select(4), .width(32)) multiplexer_4 (
    .in0(x0), .in1(ra), .in2(sp), .in3(gp), .in4(tp), .in5(t0), .in6(t1), .in7(t2), .in8(s0), .in9(s1),
    .in10(a0), .in11(a1), .in12(a2), .in13(a3), .in14(a4), .in15(a5), .out(mux21), .sel(ReadIndex2[3:0]));
  Multiplexer #(.width(32)) multiplexer_5 (.in0(mux21), .in1(mux22), .out(ReadData2), .sel(ReadIndex2[4]));
  Multiplexer #(.select(4), .width(32)) multiplexer_6 (
    .in0(a6), .in1(a7), .in2(s2), .in3(s3), .in4(s4), .in5(s5), .in6(s6), .in7(s7), .in8(s8), .in9(s9),
    .in10(s10), .in11(s11), .in12(t3), .in13(t4), .in14(t5), .in15(t6), .out(mux22), .sel(ReadIndex2[3:0]));
  Demultiplexer #(.select(5)) demultiplexer_1 (
    .out0(x0w), .out1(x1w), .out2(x2w), .out3(x3w), .out4(x4w), .out5(x5w), .out6(x6w), .out7(x7w),
    .out8(x8w), .out9(x9w), .out10(x10w), .out11(x11w), .out12(x12w), .out13(x13w), .out14(x14w),
    .out15(x15w), .out16(x16w), .out17(x17w), .out18(x18w), .out19(x19w), .out20(x20w), .out21(x21w),
    .out22(x22w), .out23(x23w), .out24(x24w), .out25(x25w), .out26(x26w), .out27(x27w), .out28(x28w),
    .out29(x29w), .out30(x30w), .out31(x31w), .in(RegWEn), .sel(WriteIndex));

  // Other names for the same wires on the sheet: sel0123[3:0] = ReadIndex1[3:0]; sel4 = ReadIndex1[4];
  //   sel20123[3:0] = ReadIndex2[3:0]; sel24 = ReadIndex2[4]

  // Notes on the sheet:
  //   INPUTS to your circuit
  //   DON'T CHANGE THE LOCATIONS OF THE INPUTS AND OUTPUTS!
  //   These are DEBUG/TEST outputs from your circuit.
  //   OUTPUTS from your circuit
endmodule
